# Fritzing sketch WemosD1Mini-Pisca-Pisca (saved by Fritzing 0.9.3b)
circuit board: 4.2339cm x 3.95302cm
breadboards: 1

parts:
  WeMos_D1_Mini1 = WeMos D1 Mini
  Power_plug1 = Power plug
  LED1 = LED - 5mm [color="Red (633nm)" package="5 mm [THT]"]
  R1 = Resistor [tolerance=±5% resistance=220 package=THT]

nets:
  3.3V: WeMos_D1_Mini1.3V3, Power_plug1.VCC
  N1: WeMos_D1_Mini1.D1, R1.Pin_0
  GND: WeMos_D1_Mini1.G, Power_plug1.GND, LED1.cathode
  N2: LED1.anode, R1.Pin_1

// code stored in the sketch: WemosD1Mini-Pisca-Pisca.ino
// https://github.com/Tucotronics/wemos-pisca/blob/master/src/wemosD1Mini-Pisca/wemosD1Mini-Pisca.ino
